// Logisim project Projeto_CVA.circ as structural Verilog: 8 circuits, main circuit BuscaInstrucao
module main (
  input  in_1
);

  wire alusrc, ALUzero, and_1_out, and_2_out, and_3_out, branch, branchlt, branchne, clk, jal, memread,
       memtoreg, memwrite, not_1_out, rg;
  wire [0:0] or_1_out;
  wire [1:0] immsel;
  wire [2:0] ALUOP, funct, rd, rs1, rs2;
  wire [3:0] opcode;
  wire [5:0] imm_b, imm_i, imm_s;
  wire [7:0] alusrcdata, data, imediato, memdata, nextpc, pc, pc_2, pc_imm, rd1, rd2, regdata, shifter_1_out;
  wire [8:0] imm_J;
  wire [15:0] buscainstrucao_1_instrucao;

  Clock clock_1 (.out(clk));
  BuscaInstrucao buscainstrucao_1 (
    .nextpc(nextpc), .clk(clk), .rst(in_1), .currentpc(pc), .Instrucao(buscainstrucao_1_instrucao));
  // Probe on buscainstrucao_1_instrucao
  // Probe on pc
  DecodificacaoInstrucao decodificacaoinstrucao_1 (
    .instrucao(buscainstrucao_1_instrucao), .opcode(opcode), .rd(rd), .funct(funct), .rs2(rs2), .rs1(rs1),
    .imm_i(imm_i), .imm_s(imm_s), .imm_b(imm_b), .imm_J(imm_J));
  bancoRegistradores bancoregistradores_1 (
    .rs1(rs1), .rs2(rs2), .rd(rd), .data(regdata), .regwrite(rg), .clk(clk), .rst(in_1), .rd1(rd1), .rd2(rd2));
  // Probe on imediato
  imm_gen imm_gen_1 (.immsel(immsel), .imm_i(imm_i), .imm_s(imm_s), .imm_b(imm_b), .imm_J(imm_J), .imediato(imediato));
  UC uc_1 (
    .opcode(opcode), .funct(funct), .clock(clk), .immsel(immsel), .alusrc(alusrc), .aluop(ALUOP),
    .branch(branch), .branchne(branchne), .branchlt(branchlt), .jal(jal), .memread(memread),
    .memtoreg(memtoreg), .memwrite(memwrite), .regwrite(rg));
  ULA ula_1 (.src1(rd1), .src2(alusrcdata), .ALUoperation(ALUOP), .ALUzero(ALUzero), .result(data));
  not not_1 (not_1_out, ALUzero);
  // Probe on data
  // Probe on rd2
  Multiplexer #(.width(8)) multiplexer_1 (.in0(rd2), .in1(imediato), .out(alusrcdata), .sel(alusrc));
  Shifter shifter_1 (.in(imediato), .\dist (3'b001), .out(shifter_1_out));
  // Probe on pc_2
  Adder adder_1 (.a(8'h2), .b(pc), .out(pc_2));  // open: cin, cout
  and and_1 (and_1_out, branch, ALUzero);
  and and_2 (and_2_out, branchne, not_1_out);
  and and_3 (and_3_out, branchlt, data[7]);
  // Probe on alusrcdata
  Adder adder_2 (.a(pc), .b(shifter_1_out), .out(pc_imm));  // open: cin, cout
  or or_1 (or_1_out[0], and_1_out, and_2_out, and_3_out);
  // Probe on pc_imm
  Multiplexer #(.select(2), .width(8)) multiplexer_2 (
    .in0(pc_2), .in1(pc_imm), .in2(pc_imm), .out(nextpc), .sel({jal, or_1_out[0]}));  // open: in3
  Multiplexer #(.select(2), .width(8)) multiplexer_3 (
    .in0(data), .in1(memdata), .in2(pc_2), .out(regdata), .sel({jal, memtoreg}));  // open: in3
  // Probe on memdata
  DM dm_1 (.address(data), .writedata(rd2), .writeEnable(memwrite), .memread(memread), .clk(clk), .ReadData(memdata));

  // Other names for the same wires on the sheet: rst = in_1
endmodule

module BuscaInstrucao (
  input  [7:0] nextpc,
  input  clk,
  input  rst,
  output [7:0] currentpc,
  output [15:0] Instrucao
);

  Register PC (.D(nextpc), .en(1'b1), .clk(clk), .Q(currentpc), .clr(rst));
  // ROM #(.line("dual")) rom_1: pin names not known; wires that end beside it: currentpc, Instrucao[15:8], Instrucao[7:0]

  // Notes on the sheet:
  //   contents of rom_1 (hex, n*v repeats v):
  //   1a 11 23 40 25 44 27 43 18 a 1a 14 85 4 8a 86 1c c0 60 5 1e 1 c 7e 60 2 7c 41 18 1e 79 2 8d 2 d 0 1e
  //   11 3d d2 7b 81 18 3 9 a6 d 60 3d d1 61 e7
endmodule

module DecodificacaoInstrucao (
  input  [15:0] instrucao,
  output [3:0] opcode,
  output [2:0] rd,
  output [2:0] funct,
  output [2:0] rs2,
  output [2:0] rs1,
  output [5:0] imm_i,
  output [5:0] imm_s,
  output [5:0] imm_b,
  output [8:0] imm_J
);

  wire comparator_2_eq, comparator_3_eq, comparator_4_eq, is_b;
  wire [0:0] comparator_1_eq;

  Comparator #(.width(4)) comparator_1 (.a(instrucao[15:12]), .b(4'b0011), .eq(comparator_1_eq[0]));  // open: gt, lt
  Comparator #(.width(4)) comparator_2 (.a(instrucao[15:12]), .b(4'b0100), .eq(comparator_2_eq));  // open: gt, lt
  Comparator #(.width(4)) comparator_3 (.a(instrucao[15:12]), .b(4'b0101), .eq(comparator_3_eq));  // open: gt, lt
  Comparator #(.width(4)) comparator_4 (.a(instrucao[15:12]), .b(4'b1000), .eq(comparator_4_eq));  // open: gt, lt
  Multiplexer #(.select(2), .width(3)) multiplexer_1 (
    .in0(instrucao[5:3]), .in1(instrucao[11:9]), .in2(instrucao[8:6]), .out(rs2),
    .sel({is_b, comparator_1_eq[0]}));  // open: in3
  or or_1 (is_b, comparator_2_eq, comparator_3_eq, comparator_4_eq);
  Multiplexer #(.width(3)) multiplexer_2 (.in0(instrucao[8:6]), .in1(instrucao[11:9]), .out(rs1), .sel(is_b));

  assign funct = instrucao[2:0];
  assign imm_b = instrucao[5:0];
  assign imm_i = instrucao[5:0];
  assign imm_J = instrucao[8:0];
  assign imm_s = instrucao[5:0];
  assign opcode = instrucao[15:12];
  assign rd = instrucao[11:9];

  // Other names for the same wires on the sheet: bits3a5[2:0] = instrucao[5:3]; bits6a8[2:0] = instrucao[8:6]

  // Notes on the sheet:
  //   imediato i
  //   imediato_s
  //   imediato_b
  //   imediato_J
endmodule

module bancoRegistradores (
  input  [2:0] rs1,
  input  [2:0] rs2,
  input  [2:0] rd,
  input  [7:0] data,
  input  regwrite,
  input  clk,
  input  rst,
  output [7:0] rd1,
  output [7:0] rd2
);

  wire we_x1, we_x2, we_x3, we_x4, we_x5, we_x6, we_x7;
  wire [7:0] q_x0, q_x1, q_x2, q_x3, q_x4, q_x5, q_x6, q_x7;

  Demultiplexer #(.select(3)) demultiplexer_1 (
    .out1(we_x1), .out2(we_x2), .out3(we_x3), .out4(we_x4), .out5(we_x5), .out6(we_x6), .out7(we_x7),
    .in(regwrite), .sel(rd));  // open: out0
  Register R0 (.D({8{1'b0}}), .clk(clk), .Q(q_x0), .clr(rst));  // open: en
  Register R4 (.D(data), .en(we_x4), .clk(clk), .Q(q_x4), .clr(rst));
  Register R1 (.D(data), .en(we_x1), .clk(clk), .Q(q_x1), .clr(rst));
  Register R5 (.D(data), .en(we_x5), .clk(clk), .Q(q_x5), .clr(rst));
  Multiplexer #(.select(3), .width(8)) multiplexer_1 (
    .in0(q_x0), .in1(q_x1), .in2(q_x2), .in3(q_x3), .in4(q_x4), .in5(q_x5), .in6(q_x6), .in7(q_x7),
    .out(rd1), .sel(rs1));
  Register R2 (.D(data), .en(we_x2), .clk(clk), .Q(q_x2), .clr(rst));
  Register R6 (.D(data), .en(we_x6), .clk(clk), .Q(q_x6), .clr(rst));
  Multiplexer #(.select(3), .width(8)) multiplexer_2 (
    .in0(q_x0), .in1(q_x1), .in2(q_x2), .in3(q_x3), .in4(q_x4), .in5(q_x5), .in6(q_x6), .in7(q_x7),
    .out(rd2), .sel(rs2));
  Register R3 (.D(data), .en(we_x3), .clk(clk), .Q(q_x3), .clr(rst));
  Register R7 (.D(data), .en(we_x7), .clk(clk), .Q(q_x7), .clr(rst));
endmodule

module ULA (
  input  [7:0] src1,
  input  [7:0] src2,
  input  [2:0] ALUoperation,
  output ALUzero,
  output [7:0] result
);

  wire comparator_1_lt;
  wire [7:0] add, and_logic, or_logic, sll_logic, slr_logic, slt_logic, sub;

  Adder adder_1 (.a(src1), .b(src2), .out(add));  // open: cin, cout
  Subtractor subtractor_1 (.a(src1), .b(src2), .out(sub));  // open: bin, bout
  assign or_logic = src1 | src2;  // OR_Gate or_1, 8 bits wide
  assign and_logic = src1 & src2;  // AND_Gate and_1, 8 bits wide
  Comparator comparator_1 (.a(src1), .b(src2), .lt(comparator_1_lt));  // open: gt, eq
  Shifter shifter_1 (.in(src1), .\dist (src2[2:0]), .out(sll_logic));
  Shifter #(.shift("lr")) shifter_2 (.in(src1), .\dist (src2[2:0]), .out(slr_logic));
  assign slt_logic = {{7{1'b0}}, comparator_1_lt};  // Bit_Extender bit_extender_1
  Multiplexer #(.select(3), .width(8)) multiplexer_1 (
    .in0(add), .in1(sub), .in2(and_logic), .in3(or_logic), .in4(slt_logic), .in5(sll_logic), .in6(slr_logic),
    .out(result), .sel(ALUoperation));  // open: in7
  Comparator comparator_2 (.a({8{1'b0}}), .b(result), .eq(ALUzero));  // open: gt, lt

  // Other names for the same wires on the sheet: ALUOP[2:0] = ALUoperation; zero = ALUzero
endmodule

module imm_gen (
  input  [1:0] immsel,
  input  [5:0] imm_i,
  input  [5:0] imm_s,
  input  [5:0] imm_b,
  input  [8:0] imm_J,
  output [7:0] imediato
);

  wire [7:0] b_16b, i_16b, J_16b, s_16b;

  assign i_16b = {{2{imm_i[5]}}, imm_i};  // Bit_Extender bit_extender_1
  assign s_16b = {{2{1'b0}}, imm_s};  // Bit_Extender bit_extender_2
  assign b_16b = {{2{imm_b[5]}}, imm_b};  // Bit_Extender bit_extender_3
  Bit_Extender #(.in_width(9), .out_width(8)) bit_extender_4 (.in(imm_J), .out(J_16b));
  Multiplexer #(.select(2), .width(8)) multiplexer_1 (
    .in0(i_16b), .in1(s_16b), .in2(b_16b), .in3(J_16b), .out(imediato), .sel(immsel));

  // Other names for the same wires on the sheet: imm[7:0] = imediato

  // Notes on the sheet:
  //   instrucao tipo i
  //   instrucao tipo s
  //   instrucao tipo b
  //   instrucao tipo J
endmodule

module UC (
  input  [3:0] opcode,
  input  [2:0] funct,
  input  clock,
  output [1:0] immsel,
  output alusrc,
  output [2:0] aluop,
  output branch,
  output branchne,
  output branchlt,
  output jal,
  output memread,
  output memtoreg,
  output memwrite,
  output regwrite
);

  wire is_b, is_i, tipo_i_ar, tipo_i_slli, tipo_r;
  wire [2:0] multiplexer_1_out, multiplexer_2_out;

  or or_1 (immsel[0], memwrite, jal);
  or or_2 (immsel[1], is_b, jal);
  or or_3 (is_b, branch, branchne, branchlt);
  // Probe on immsel
  or or_4 (is_i, tipo_i_ar, memread, tipo_i_slli);
  or or_5 (alusrc, memwrite, is_i);
  Decoder #(.select(4)) decoder_1 (
    .out0(tipo_r), .out1(tipo_i_ar), .out2(memread), .out3(memwrite), .out4(branch), .out5(branchne),
    .out6(jal), .out7(tipo_i_slli), .out8(branchlt), .sel(opcode), .en(1'b1));  // open: out9, out10, out11, out12, out13, out14, out15
  // Probe on alusrc
  Multiplexer #(.width(3)) multiplexer_1 (.in0(3'b000), .in1(3'b001), .out(multiplexer_1_out), .sel(is_b));
  // Probe on aluop
  Multiplexer #(.width(3)) multiplexer_2 (.in0(multiplexer_1_out), .in1(funct), .out(multiplexer_2_out), .sel(tipo_r));
  Multiplexer #(.width(3)) multiplexer_3 (.in0(multiplexer_2_out), .in1(3'b101), .out(aluop), .sel(tipo_i_slli));
  or or_6 (regwrite, tipo_r, is_i, jal);

  assign memtoreg = memread;

  // Other names for the same wires on the sheet: tipo_b_beq = branch; tipo_b_blt = branchlt; tipo_b_bne = branchne;
  //   tipo_i_lw = memread; tipo_J = jal; tipo_s = memwrite

  // Notes on the sheet:
  //   immsel
  //   Tipo I - 00
  //   Tipo s - 01
  //   Tipo b - 10
  //   Tipo j - 11
  //   alusrc
  //   aluop
  //   regwrite
endmodule

module DM (
  input  [7:0] address,
  input  [7:0] writedata,
  input  writeEnable,
  input  memread,
  input  clk,
  output [7:0] ReadData
);

  wire [7:0] ram_1_dout;

  RAM #(.asyncread("true"), .trigger("falling")) ram_1 (
    .addr(address), .we(writeEnable), .oe(memread), .clk(clk), .din(writedata), .dout(ram_1_dout));
  assign ReadData = memread ? ram_1_dout : 8'bz;  // Controlled_Buffer controlled_buffer_1

  // Other names for the same wires on the sheet: mr = memread; we = writeEnable
endmodule
