// Logisim project Projeto_SFI_main.circ as structural Verilog: 8 circuits, main circuit BuscaInstrucao
module main (
  input  in_1,
  input  [7:0] data
);

  wire alusrc, ALUzero, and_1_out, and_2_out, branch, branchne, clk, clock_1_out, comparator_1_eq,
       comparator_2_eq, decoder_1_out0, decoder_1_out1, decoder_1_out2, decoder_1_out3, decoder_1_out4,
       decoder_1_out5, decoder_1_out6, demultiplexer_1_out1, demultiplexer_1_out2, demultiplexer_1_out3,
       demultiplexer_1_out4, demultiplexer_1_out5, demultiplexer_1_out6, demultiplexer_1_out7, is_b, jal,
       memread, memtoreg, memwrite, not_1_out, or_3_out, or_6_out, or_8_out;
  wire [0:0] comparator_3_eq, or_1_out;
  wire [1:0] immsel;
  wire [2:0] ALUOP, aluop_t, funct, multiplexer_3_out, multiplexer_5_out, multiplexer_6_out;
  wire [3:0] rom_1_p2_2;
  wire [3:1] rom_1_p2;
  wire [5:0] imm_b;
  wire [7:0] adder_1_out, adder_2_out, alusrcdata, imediato, memdata, multiplexer_1_out, pc_2, PC_q, R0_q,
       R1_q, R2_q, R3_q, R4_q, R5_q, R6_q, R7_q, rd1, rd2, regdata, shifter_1_out;
  wire [8:6] imm_J;

  Clock clock_1 (.out(clock_1_out));
  Register PC (.D(multiplexer_1_out), .en(1'b1), .clk(clock_1_out), .Q(PC_q), .clr(in_1));
  Shifter shifter_1 (.in(imediato), .\dist (3'b001), .out(shifter_1_out));
  // ROM #(.line("dual")) rom_1: pin names not known; wires that end beside it: PC_q, {rom_1_p2_2, rom_1_p2, imm_J[8]}, {imm_J[7:6], imm_b}
  not not_1 (not_1_out, ALUzero);
  // Probe on adder_1_out
  Adder adder_1 (.a(PC_q), .b(shifter_1_out), .out(adder_1_out));  // open: cin, cout
  and and_1 (and_1_out, branch, ALUzero);
  and and_2 (and_2_out, branchne, not_1_out);
  Adder adder_2 (.a(8'h2), .b(PC_q), .out(adder_2_out));  // open: cin, cout
  or or_1 (or_1_out[0], and_1_out, and_2_out);
  Multiplexer #(.select(2), .width(8)) multiplexer_1 (
    .in0(adder_2_out), .in1(adder_1_out), .in2(adder_1_out), .out(multiplexer_1_out), .sel({jal, or_1_out[0]}));  // open: in3
  Demultiplexer #(.select(3)) demultiplexer_1 (
    .out1(demultiplexer_1_out1), .out2(demultiplexer_1_out2), .out3(demultiplexer_1_out3),
    .out4(demultiplexer_1_out4), .out5(demultiplexer_1_out5), .out6(demultiplexer_1_out6),
    .out7(demultiplexer_1_out7), .in(or_8_out), .sel(rom_1_p2));  // open: out0
  Comparator #(.width(4)) comparator_1 (.a(rom_1_p2_2), .b(4'b0100), .eq(comparator_1_eq));  // open: gt, lt
  Comparator #(.width(4)) comparator_2 (.a(rom_1_p2_2), .b(4'b0101), .eq(comparator_2_eq));  // open: gt, lt
  Register R0 (.D({8{1'b0}}), .clk(clock_1_out), .Q(R0_q), .clr(in_1));  // open: en
  Register R4 (.D(data), .en(demultiplexer_1_out4), .clk(clock_1_out), .Q(R4_q), .clr(in_1));
  Multiplexer #(.select(3), .width(8)) multiplexer_2 (
    .in0(R0_q), .in1(R1_q), .in2(R2_q), .in3(R3_q), .in4(R4_q), .in5(R5_q), .in6(R6_q), .in7(R7_q),
    .out(rd2), .sel(multiplexer_3_out));
  or or_2 (is_b, comparator_1_eq, comparator_2_eq);
  Multiplexer #(.select(2), .width(3)) multiplexer_3 (
    .in0(imm_b[5:3]), .in1(rom_1_p2), .in2(imm_J), .out(multiplexer_3_out), .sel({is_b, comparator_3_eq[0]}));  // open: in3
  Comparator #(.width(4)) comparator_3 (.a(rom_1_p2_2), .b(4'b0011), .eq(comparator_3_eq[0]));  // open: gt, lt
  Register R1 (.D(data), .en(demultiplexer_1_out1), .clk(clock_1_out), .Q(R1_q), .clr(in_1));
  Register R5 (.D(data), .en(demultiplexer_1_out5), .clk(clock_1_out), .Q(R5_q), .clr(in_1));
  Multiplexer #(.select(3), .width(8)) multiplexer_4 (
    .in0(R0_q), .in1(R1_q), .in2(R2_q), .in3(R3_q), .in4(R4_q), .in5(R5_q), .in6(R6_q), .in7(R7_q),
    .out(rd1), .sel(multiplexer_5_out));
  Multiplexer #(.width(3)) multiplexer_5 (.in0(imm_J), .in1(rom_1_p2), .out(multiplexer_5_out), .sel(is_b));
  Register R2 (.D(data), .en(demultiplexer_1_out2), .clk(clock_1_out), .Q(R2_q), .clr(in_1));
  Register R6 (.D(data), .en(demultiplexer_1_out6), .clk(clock_1_out), .Q(R6_q), .clr(in_1));
  Register R3 (.D(data), .en(demultiplexer_1_out3), .clk(clock_1_out), .Q(R3_q), .clr(in_1));
  Register R7 (.D(data), .en(demultiplexer_1_out7), .clk(clock_1_out), .Q(R7_q), .clr(in_1));
  or or_3 (or_3_out, decoder_1_out4, decoder_1_out5);
  or or_4 (immsel[0], decoder_1_out3, decoder_1_out6);
  or or_5 (immsel[1], or_3_out, decoder_1_out6);
  or or_6 (or_6_out, decoder_1_out1, decoder_1_out2);
  // Probe on immsel
  Decoder #(.select(4)) decoder_1 (
    .out0(decoder_1_out0), .out1(decoder_1_out1), .out2(decoder_1_out2), .out3(decoder_1_out3),
    .out4(decoder_1_out4), .out5(decoder_1_out5), .out6(decoder_1_out6), .sel(rom_1_p2_2), .en(1'b1));  // open: out7, out8, out9, out10, out11, out12, out13, out14, out15
  or or_7 (alusrc, decoder_1_out3, or_6_out);
  // Probe on alusrc
  Multiplexer #(.width(3)) multiplexer_6 (.in0(3'b000), .in1(3'b001), .out(multiplexer_6_out), .sel(or_3_out));
  Multiplexer #(.width(3)) multiplexer_7 (.in0(multiplexer_6_out), .in1(funct), .out(aluop_t), .sel(decoder_1_out0));
  // Probe on aluop_t
  or or_8 (or_8_out, decoder_1_out0, or_6_out, decoder_1_out6);
  imm_gen imm_gen_1 (
    .immsel(immsel), .imm_i(imm_b), .imm_s(imm_b), .imm_b(imm_b), .imm_J({imm_J, imm_b}), .imediato(imediato));
  // Probe on imediato
  // Probe on rd2
  ULA ula_1 (.src1(rd1), .src2(alusrcdata), .ALUoperation(ALUOP), .ALUzero(ALUzero), .result(data));
  // Probe on alusrcdata
  Multiplexer #(.width(8)) multiplexer_8 (.in0(rd2), .in1(imediato), .out(alusrcdata), .sel(alusrc));
  DM dm_1 (.address(data), .writedata(rd2), .writeEnable(memwrite), .memread(memread), .clk(clk), .ReadData(memdata));
  Multiplexer #(.select(2), .width(8)) multiplexer_9 (
    .in0(data), .in1(memdata), .in2(pc_2), .out(regdata), .sel({jal, memtoreg}));  // open: in3
  // Probe on memdata

  // Other names for the same wires on the sheet: imm_i[5:0] = imm_b; imm_J[5:0] = imm_b; imm_s[5:0] = imm_b

  // Notes on the sheet:
  //   contents of rom_1 (hex, n*v repeats v):
  //   22 10 24 11 26 12 28 13 a 5c 4a 9 b 14 4a 4 1c 2 1e 2 60 6 1c 1 1e 1 60 3 1c 0 1e 0 3c 20 3e 21 61
  //   ee
  //   imediato i
  //   imediato_s
  //   imediato_b
  //   imediato_J
  //   immsel
  //   Tipo I - 00
  //   Tipo s - 01
  //   Tipo b - 10
  //   Tipo j - 11
  //   alusrc
  //   aluop
  //   regwrite
endmodule

module BuscaInstrucao (
  input  [7:0] nextpc,
  input  clk,
  input  rst,
  output [7:0] currentpc,
  output [15:0] Instrucao
);

  Register PC (.D(nextpc), .en(1'b1), .clk(clk), .Q(currentpc), .clr(rst));
  // ROM #(.line("dual")) rom_1: pin names not known; wires that end beside it: currentpc, Instrucao[15:8], Instrucao[7:0]

  // Notes on the sheet:
  //   contents of rom_1 (hex, n*v repeats v):
  //   22 10 24 11 26 12 28 13 a 5c 4a 9 b 14 4a 4 1c 2 1e 2 60 6 1c 1 1e 1 60 3 1c 0 1e 0 3c 20 3e 21 61
  //   ee
endmodule

module DecodificacaoInstrucao (
  input  [15:0] instrucao,
  output [3:0] opcode,
  output [2:0] rd,
  output [2:0] funct,
  output [2:0] rs2,
  output [2:0] rs1,
  output [5:0] imm_i,
  output [5:0] imm_s,
  output [5:0] imm_b,
  output [8:0] imm_J
);

  wire comparator_2_eq, comparator_3_eq, is_b;
  wire [0:0] comparator_1_eq;

  Comparator #(.width(4)) comparator_1 (.a(instrucao[15:12]), .b(4'b0011), .eq(comparator_1_eq[0]));  // open: gt, lt
  Comparator #(.width(4)) comparator_2 (.a(instrucao[15:12]), .b(4'b0100), .eq(comparator_2_eq));  // open: gt, lt
  Comparator #(.width(4)) comparator_3 (.a(instrucao[15:12]), .b(4'b0101), .eq(comparator_3_eq));  // open: gt, lt
  Multiplexer #(.select(2), .width(3)) multiplexer_1 (
    .in0(instrucao[5:3]), .in1(instrucao[11:9]), .in2(instrucao[8:6]), .out(rs2),
    .sel({is_b, comparator_1_eq[0]}));  // open: in3
  or or_1 (is_b, comparator_2_eq, comparator_3_eq);
  Multiplexer #(.width(3)) multiplexer_2 (.in0(instrucao[8:6]), .in1(instrucao[11:9]), .out(rs1), .sel(is_b));

  assign funct = instrucao[2:0];
  assign imm_b = instrucao[5:0];
  assign imm_i = instrucao[5:0];
  assign imm_J = instrucao[8:0];
  assign imm_s = instrucao[5:0];
  assign opcode = instrucao[15:12];
  assign rd = instrucao[11:9];

  // Other names for the same wires on the sheet: bits3a5[2:0] = instrucao[5:3]; bits6a8[2:0] = instrucao[8:6]

  // Notes on the sheet:
  //   imediato i
  //   imediato_s
  //   imediato_b
  //   imediato_J
endmodule

module bancoRegistradores (
  input  [2:0] rs1,
  input  [2:0] rs2,
  input  [2:0] rd,
  input  [7:0] data,
  input  regwrite,
  input  clk,
  input  rst,
  output [7:0] rd1,
  output [7:0] rd2
);

  wire we_x1, we_x2, we_x3, we_x4, we_x5, we_x6, we_x7;
  wire [7:0] q_x0, q_x1, q_x2, q_x3, q_x4, q_x5, q_x6, q_x7;

  Demultiplexer #(.select(3)) demultiplexer_1 (
    .out1(we_x1), .out2(we_x2), .out3(we_x3), .out4(we_x4), .out5(we_x5), .out6(we_x6), .out7(we_x7),
    .in(regwrite), .sel(rd));  // open: out0
  Register R0 (.D({8{1'b0}}), .clk(clk), .Q(q_x0), .clr(rst));  // open: en
  Register R4 (.D(data), .en(we_x4), .clk(clk), .Q(q_x4), .clr(rst));
  Register R1 (.D(data), .en(we_x1), .clk(clk), .Q(q_x1), .clr(rst));
  Register R5 (.D(data), .en(we_x5), .clk(clk), .Q(q_x5), .clr(rst));
  Multiplexer #(.select(3), .width(8)) multiplexer_1 (
    .in0(q_x0), .in1(q_x1), .in2(q_x2), .in3(q_x3), .in4(q_x4), .in5(q_x5), .in6(q_x6), .in7(q_x7),
    .out(rd1), .sel(rs1));
  Register R2 (.D(data), .en(we_x2), .clk(clk), .Q(q_x2), .clr(rst));
  Register R6 (.D(data), .en(we_x6), .clk(clk), .Q(q_x6), .clr(rst));
  Multiplexer #(.select(3), .width(8)) multiplexer_2 (
    .in0(q_x0), .in1(q_x1), .in2(q_x2), .in3(q_x3), .in4(q_x4), .in5(q_x5), .in6(q_x6), .in7(q_x7),
    .out(rd2), .sel(rs2));
  Register R3 (.D(data), .en(we_x3), .clk(clk), .Q(q_x3), .clr(rst));
  Register R7 (.D(data), .en(we_x7), .clk(clk), .Q(q_x7), .clr(rst));
endmodule

module ULA (
  input  [7:0] src1,
  input  [7:0] src2,
  input  [2:0] ALUoperation,
  output ALUzero,
  output [7:0] result
);

  wire comparator_1_lt;
  wire [7:0] add, and_logic, or_logic, slt_logic, sub;

  Adder adder_1 (.a(src1), .b(src2), .out(add));  // open: cin, cout
  Subtractor subtractor_1 (.a(src1), .b(src2), .out(sub));  // open: bin, bout
  assign or_logic = src1 | src2;  // OR_Gate or_1, 8 bits wide
  assign and_logic = src1 & src2;  // AND_Gate and_1, 8 bits wide
  Comparator comparator_1 (.a(src1), .b(src2), .lt(comparator_1_lt));  // open: gt, eq
  assign slt_logic = {{7{1'b0}}, comparator_1_lt};  // Bit_Extender bit_extender_1
  Multiplexer #(.select(3), .width(8)) multiplexer_1 (
    .in0(add), .in1(sub), .in2(and_logic), .in3(or_logic), .in4(slt_logic), .in5({8{1'b0}}), .in6({8{1'b0}}),
    .in7({8{1'b0}}), .out(result), .sel(ALUoperation));
  Comparator comparator_2 (.a({8{1'b0}}), .b(result), .eq(ALUzero));  // open: gt, lt

  // Other names for the same wires on the sheet: ALUOP[2:0] = ALUoperation; zero = ALUzero
endmodule

module imm_gen (
  input  [1:0] immsel,
  input  [5:0] imm_i,
  input  [5:0] imm_s,
  input  [5:0] imm_b,
  input  [8:0] imm_J,
  output [7:0] imediato
);

  wire [7:0] b_16b, i_16b, J_16b, s_16b;

  assign i_16b = {{2{imm_i[5]}}, imm_i};  // Bit_Extender bit_extender_1
  assign s_16b = {{2{1'b0}}, imm_s};  // Bit_Extender bit_extender_2
  assign b_16b = {{2{imm_b[5]}}, imm_b};  // Bit_Extender bit_extender_3
  Bit_Extender #(.in_width(9), .out_width(8)) bit_extender_4 (.in(imm_J), .out(J_16b));
  Multiplexer #(.select(2), .width(8)) multiplexer_1 (
    .in0(i_16b), .in1(s_16b), .in2(b_16b), .in3(J_16b), .out(imediato), .sel(immsel));

  // Other names for the same wires on the sheet: imm[7:0] = imediato

  // Notes on the sheet:
  //   instrucao tipo i
  //   instrucao tipo s
  //   instrucao tipo b
  //   instrucao tipo J
endmodule

module UC (
  input  [3:0] opcode,
  input  [2:0] funct,
  input  clock,
  output [1:0] immsel,
  output alusrc,
  output [2:0] aluop,
  output branch,
  output branchne,
  output jal,
  output memread,
  output memtoreg,
  output memwrite,
  output regwrite
);

  wire is_b, is_i, tipo_i_ar, tipo_r;
  wire [2:0] multiplexer_1_out;

  or or_1 (immsel[0], memwrite, jal);
  or or_2 (immsel[1], is_b, jal);
  or or_3 (is_b, branch, branchne);
  // Probe on immsel
  or or_4 (is_i, tipo_i_ar, memread);
  or or_5 (alusrc, memwrite, is_i);
  Decoder #(.select(4)) decoder_1 (
    .out0(tipo_r), .out1(tipo_i_ar), .out2(memread), .out3(memwrite), .out4(branch), .out5(branchne),
    .out6(jal), .sel(opcode), .en(1'b1));  // open: out7, out8, out9, out10, out11, out12, out13, out14, out15
  // Probe on alusrc
  Multiplexer #(.width(3)) multiplexer_1 (.in0(3'b000), .in1(3'b001), .out(multiplexer_1_out), .sel(is_b));
  // Probe on aluop
  Multiplexer #(.width(3)) multiplexer_2 (.in0(multiplexer_1_out), .in1(funct), .out(aluop), .sel(tipo_r));
  or or_6 (regwrite, tipo_r, is_i, jal);

  assign memtoreg = memread;

  // Other names for the same wires on the sheet: tipo_b_beq = branch; tipo_b_bne = branchne; tipo_i_lw = memread;
  //   tipo_J = jal; tipo_s = memwrite

  // Notes on the sheet:
  //   immsel
  //   Tipo I - 00
  //   Tipo s - 01
  //   Tipo b - 10
  //   Tipo j - 11
  //   alusrc
  //   aluop
  //   regwrite
endmodule

module DM (
  input  [7:0] address,
  input  [7:0] writedata,
  input  writeEnable,
  input  memread,
  input  clk,
  output [7:0] ReadData
);

  wire [7:0] ram_1_dout;

  RAM #(.asyncread("true"), .trigger("falling")) ram_1 (
    .addr(address), .we(writeEnable), .oe(memread), .clk(clk), .din(writedata), .dout(ram_1_dout));
  assign ReadData = memread ? ram_1_dout : 8'bz;  // Controlled_Buffer controlled_buffer_1

  // Other names for the same wires on the sheet: mr = memread; we = writeEnable
endmodule
